# Fritzing sketch scheme (saved by Fritzing 1.0.6)
breadboards: 1

parts:
  MCU1 = Raspberry Pi Zero
  LED1 = LED - 5mm [color="Red (633nm)" current=0.030A package="5 mm [THT]"]
  R1 = Resistor [tolerance=±5% resistance=220 package="2512 [SMD]"]

nets:
  N1: MCU1.pin_9, MCU1.pin_39, LED1.cathode
  N2: MCU1.pin_40, R1.Pin_0
  N3: LED1.anode, R1.Pin_1
