# Fritzing sketch scheme_music (saved by Fritzing 1.0.6)
breadboards: 1

parts:
  MCU1 = Raspberry Pi Zero
  LED1 = LED - 5mm [color="Red (633nm)" current=0.030A package="5 mm [THT]"]
  R1 = Resistor [tolerance=±5% resistance=220 package="2512 [SMD]"]
  J1 = Piezo Speaker
  R2 = Resistor [tolerance=±5% resistance=330 package="2010 [SMD]"]

nets:
  N1: MCU1.pin_9, MCU1.pin_39, LED1.cathode, J1.pin1
  N2: MCU1.pin_12, J1.pin2, R2.Pin_0, R2.Pin_1
  N3: MCU1.pin_40, R1.Pin_0
  N4: LED1.anode, R1.Pin_1
